# Fritzing sketch InputBoard (saved by Fritzing 0.9.0b)
breadboards: 1

parts:
  MUX1 = IC, DIP package, 16 pins [chip_label=74151]
  J1 = female pin header, 28 pins [form="♀ (female)"]  # not connected
  J2 = female pin header, 28 pins [form="♀ (female)"]  # not connected

nets:
  5V: MUX1.pin16
