# Fritzing sketch Output Board (saved by Fritzing 0.9.0b)
breadboards: 1

parts:
  REG1 = IC, DIP package, 20 pins [chip_label=SN74HC574]
  REG2 = IC, DIP package, 20 pins [chip_label=SN74HC574]
  REG3 = IC, DIP package, 20 pins [chip_label=SN74HC574]
  REG4 = IC, DIP package, 20 pins [chip_label=SN74HC574]
  REG5 = IC, DIP package, 20 pins [chip_label=SN74HC574]
  REG6 = IC, DIP package, 20 pins [chip_label=SN74HC574]
  REG7 = IC, DIP package, 20 pins [chip_label=SN74HC574]
  J1 = female pin header, 28 pins [form="♀ (female)"]  # not connected
  J2 = female pin header, 28 pins [form="♀ (female)"]  # not connected

nets:
  5V: REG1.pin20, REG2.pin20, REG3.pin20, REG4.pin20, REG5.pin20, REG6.pin20, REG7.pin20
